# Fritzing sketch Integration Schematics (saved by Fritzing 0.9.3b)
breadboards: 1

parts:
  ARDUINO_MEGA = Arduino Mega 2560 (Rev3)
  Altimeter_Module_MS5607 = mystery part, 7 pins [chip_label=Altitude]
  SIM33EAU_GPS_Module = mystery part, 4 pins [chip_label=GPS]
  TNC = mystery part, 4 pins [chip_label=TNC]
  POWER_SOURCE = Battery
  Adafruit_MAX31865 = mystery part, 6 pins [chip_label=Temperature]
  OV5644_Camera_Module = IC, SIP package, 8 pins [chip_label=OV5642]
  MicroSD_Module = Adafruit MicroSD card breakout board [part_number="Adafruit #254"]

nets:
  N1: ARDUINO_MEGA.D21/SCL, ARDUINO_MEGA.SCL, OV5644_Camera_Module.pin8
  N2: ARDUINO_MEGA.D20/SDA, ARDUINO_MEGA.SDA, OV5644_Camera_Module.pin7
  N3: ARDUINO_MEGA.D19/RX1, TNC.pin2
  N4: ARDUINO_MEGA.D18/TX1, TNC.pin3
  N5: ARDUINO_MEGA.D17_PWM/RX2, SIM33EAU_GPS_Module.pin1
  N6: ARDUINO_MEGA.D16_PWM/TX2, SIM33EAU_GPS_Module.pin2
  3V3: ARDUINO_MEGA.3V3, Altimeter_Module_MS5607.pin1, SIM33EAU_GPS_Module.pin3, TNC.pin1, MicroSD_Module.VCC
  N7: ARDUINO_MEGA.5V, Adafruit_MAX31865.pin1, OV5644_Camera_Module.pin6
  GND: ARDUINO_MEGA.GND, Altimeter_Module_MS5607.pin7, SIM33EAU_GPS_Module.pin4, TNC.pin4, POWER_SOURCE.-, Adafruit_MAX31865.pin6, OV5644_Camera_Module.pin5, MicroSD_Module.GND
  N8: ARDUINO_MEGA.VIN, POWER_SOURCE.+
  N9: ARDUINO_MEGA.D22, MicroSD_Module.CS
  N10: ARDUINO_MEGA.D23, Adafruit_MAX31865.pin5
  N11: ARDUINO_MEGA.D24, Altimeter_Module_MS5607.pin3
  N12: ARDUINO_MEGA.D25, OV5644_Camera_Module.pin1
  N13: ARDUINO_MEGA.D50, Altimeter_Module_MS5607.pin6, Adafruit_MAX31865.pin3, OV5644_Camera_Module.pin3, MicroSD_Module.DO
  N14: ARDUINO_MEGA.D51, Altimeter_Module_MS5607.pin5, Adafruit_MAX31865.pin4, OV5644_Camera_Module.pin2, MicroSD_Module.DI
  N15: ARDUINO_MEGA.D52, Altimeter_Module_MS5607.pin4, Adafruit_MAX31865.pin2, OV5644_Camera_Module.pin4, MicroSD_Module.CLK

custom parts:
  Battery: Your standard 2x 18650 battery pack (7,4 Volts)
  Adafruit MicroSD card breakout board: Not just a simple breakout board, this microSD adapter goes the extra mile - designed for ease of use. Onboard 5v->3v regulator provides 150mA for power-hungry cards 3v level shifting means you can use this with ease on either 3v or 5v systems Uses a proper level shifting chip, not resistors: less problems, and faster read/write access Use 3 or 4 digital pins to read and write 2Gb+ of storage!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
